// Logisim project regfile (1).circ as structural Verilog: 1 circuit, main circuit main
module main (
  input  [4:0] in_1,
  input  [4:0] in_2,
  input  [4:0] in_3,
  input  [31:0] in_4,
  input  in_5,
  input  in_6,
  input  in_7,
  output [31:0] out_8,
  output [31:0] out_9
);

  wire decoder_1_out0, decoder_1_out1, decoder_2_out0, decoder_2_out1, decoder_2_out2, decoder_2_out3,
       decoder_3_out1, decoder_3_out2, decoder_3_out3, decoder_4_out0, decoder_4_out1, decoder_4_out2,
       decoder_4_out3, decoder_5_out0, decoder_5_out1, decoder_5_out2, decoder_5_out3, decoder_6_out0,
       decoder_6_out1, decoder_6_out2, decoder_6_out3, decoder_7_out0, decoder_7_out1, decoder_7_out2,
       decoder_7_out3, decoder_8_out0, decoder_8_out1, decoder_8_out2, decoder_8_out3, decoder_9_out0,
       decoder_9_out1, decoder_9_out2, decoder_9_out3, decoder_10_out0, decoder_10_out1, decoder_10_out2,
       decoder_10_out3, decoder_11_out0, decoder_11_out1, decoder_11_out2, decoder_11_out3;
  wire [31:0] multiplexer_1_out, multiplexer_2_out, multiplexer_3_out, multiplexer_4_out, multiplexer_5_out,
       multiplexer_6_out, multiplexer_7_out, multiplexer_8_out, multiplexer_9_out, multiplexer_10_out,
       multiplexer_11_out, multiplexer_12_out, multiplexer_13_out, register_1_q, register_2_q, register_3_q,
       register_4_q, register_5_q, register_6_q, register_7_q, register_8_q, register_9_q, register_10_q,
       register_11_q, register_12_q, register_13_q, register_14_q, register_15_q, register_16_q,
       register_17_q, register_18_q, register_19_q, register_20_q, register_21_q, register_22_q,
       register_23_q, register_24_q, register_25_q, register_26_q, register_27_q, register_28_q,
       register_29_q, register_30_q, register_31_q, register_32_q;

  // Probe on in_3
  Decoder decoder_1 (.out0(decoder_1_out0), .out1(decoder_1_out1), .sel(in_3[4]), .en(in_5));
  Decoder #(.select(2), .disabled(0)) decoder_2 (
    .out0(decoder_2_out0), .out1(decoder_2_out1), .out2(decoder_2_out2), .out3(decoder_2_out3),
    .sel(in_3[3:2]), .en(decoder_1_out0));
  Decoder #(.select(2), .disabled(0)) decoder_3 (
    .out1(decoder_3_out1), .out2(decoder_3_out2), .out3(decoder_3_out3), .sel(in_3[1:0]), .en(decoder_2_out0));  // open: out0
  Decoder #(.select(2), .disabled(0)) decoder_4 (
    .out0(decoder_4_out0), .out1(decoder_4_out1), .out2(decoder_4_out2), .out3(decoder_4_out3),
    .sel(in_3[1:0]), .en(decoder_2_out1));
  Decoder #(.select(2), .disabled(0)) decoder_5 (
    .out0(decoder_5_out0), .out1(decoder_5_out1), .out2(decoder_5_out2), .out3(decoder_5_out3),
    .sel(in_3[1:0]), .en(decoder_2_out2));
  Decoder #(.select(2), .disabled(0)) decoder_6 (
    .out0(decoder_6_out0), .out1(decoder_6_out1), .out2(decoder_6_out2), .out3(decoder_6_out3),
    .sel(in_3[1:0]), .en(decoder_2_out3));
  Multiplexer #(.width(32), .disabled(0), .enable("false")) multiplexer_1 (
    .in1(in_4), .out(multiplexer_1_out), .sel(in_5));  // open: in0
  Register #(.width(32)) register_1 (.D({32{1'b0}}), .Q(register_1_q), .clk(in_6), .clr(in_7));  // open: en
  Register #(.width(32)) register_2 (
    .D(multiplexer_1_out), .en(decoder_3_out1), .Q(register_2_q), .clk(in_6), .clr(in_7));
  Register #(.width(32)) register_3 (
    .D(multiplexer_1_out), .en(decoder_3_out2), .Q(register_3_q), .clk(in_6), .clr(in_7));
  Register #(.width(32)) register_4 (
    .D(multiplexer_1_out), .en(decoder_3_out3), .Q(register_4_q), .clk(in_6), .clr(in_7));
  Register #(.width(32)) register_5 (
    .D(multiplexer_1_out), .en(decoder_4_out0), .Q(register_5_q), .clk(in_6), .clr(in_7));
  Register #(.width(32)) register_6 (
    .D(multiplexer_1_out), .en(decoder_4_out1), .Q(register_6_q), .clk(in_6), .clr(in_7));
  Register #(.width(32)) register_7 (
    .D(multiplexer_1_out), .en(decoder_4_out2), .Q(register_7_q), .clk(in_6), .clr(in_7));
  Register #(.width(32)) register_8 (
    .D(multiplexer_1_out), .en(decoder_4_out3), .Q(register_8_q), .clk(in_6), .clr(in_7));
  Register #(.width(32)) register_9 (
    .D(multiplexer_1_out), .en(decoder_5_out0), .Q(register_9_q), .clk(in_6), .clr(in_7));
  Register #(.width(32)) register_10 (
    .D(multiplexer_1_out), .en(decoder_5_out1), .Q(register_10_q), .clk(in_6), .clr(in_7));
  Register #(.width(32)) register_11 (
    .D(multiplexer_1_out), .en(decoder_5_out2), .Q(register_11_q), .clk(in_6), .clr(in_7));
  Register #(.width(32)) register_12 (
    .D(multiplexer_1_out), .en(decoder_5_out3), .Q(register_12_q), .clk(in_6), .clr(in_7));
  Register #(.width(32)) register_13 (
    .D(multiplexer_1_out), .en(decoder_6_out0), .Q(register_13_q), .clk(in_6), .clr(in_7));
  Register #(.width(32)) register_14 (
    .D(multiplexer_1_out), .en(decoder_6_out1), .Q(register_14_q), .clk(in_6), .clr(in_7));
  Register #(.width(32)) register_15 (
    .D(multiplexer_1_out), .en(decoder_6_out2), .Q(register_15_q), .clk(in_6), .clr(in_7));
  Register #(.width(32)) register_16 (
    .D(multiplexer_1_out), .en(decoder_6_out3), .Q(register_16_q), .clk(in_6), .clr(in_7));
  Multiplexer #(.select(3), .width(32), .enable("false")) multiplexer_2 (
    .in0(register_1_q), .in1(register_2_q), .in2(register_3_q), .in3(register_4_q), .in4(register_5_q),
    .in5(register_6_q), .in6(register_7_q), .in7(register_8_q), .out(multiplexer_2_out), .sel(in_2[2:0]));
  Multiplexer #(.select(3), .width(32), .enable("false")) multiplexer_3 (
    .in0(register_1_q), .in1(register_2_q), .in2(register_3_q), .in3(register_4_q), .in4(register_5_q),
    .in5(register_6_q), .in6(register_7_q), .in7(register_8_q), .out(multiplexer_3_out), .sel(in_1[2:0]));
  Multiplexer #(.select(3), .width(32), .enable("false")) multiplexer_4 (
    .in0(register_9_q), .in1(register_10_q), .in2(register_11_q), .in3(register_12_q), .in4(register_13_q),
    .in5(register_14_q), .in6(register_15_q), .in7(register_16_q), .out(multiplexer_4_out), .sel(in_2[2:0]));
  Multiplexer #(.select(3), .width(32), .enable("false")) multiplexer_5 (
    .in0(register_9_q), .in1(register_10_q), .in2(register_11_q), .in3(register_12_q), .in4(register_13_q),
    .in5(register_14_q), .in6(register_15_q), .in7(register_16_q), .out(multiplexer_5_out), .sel(in_1[2:0]));
  Multiplexer #(.width(32), .enable("false")) multiplexer_6 (
    .in0(multiplexer_2_out), .in1(multiplexer_4_out), .out(multiplexer_6_out), .sel(in_2[3]));
  Multiplexer #(.width(32), .enable("false")) multiplexer_7 (
    .in0(multiplexer_3_out), .in1(multiplexer_5_out), .out(multiplexer_7_out), .sel(in_1[3]));
  // Probe on in_2
  // Probe on in_1
  Decoder #(.select(2), .disabled(0)) decoder_7 (
    .out0(decoder_7_out0), .out1(decoder_7_out1), .out2(decoder_7_out2), .out3(decoder_7_out3),
    .sel(in_3[3:2]), .en(decoder_1_out1));
  Decoder #(.select(2), .disabled(0)) decoder_8 (
    .out0(decoder_8_out0), .out1(decoder_8_out1), .out2(decoder_8_out2), .out3(decoder_8_out3),
    .sel(in_3[1:0]), .en(decoder_7_out0));
  Decoder #(.select(2), .disabled(0)) decoder_9 (
    .out0(decoder_9_out0), .out1(decoder_9_out1), .out2(decoder_9_out2), .out3(decoder_9_out3),
    .sel(in_3[1:0]), .en(decoder_7_out1));
  Decoder #(.select(2), .disabled(0)) decoder_10 (
    .out0(decoder_10_out0), .out1(decoder_10_out1), .out2(decoder_10_out2), .out3(decoder_10_out3),
    .sel(in_3[1:0]), .en(decoder_7_out2));
  Decoder #(.select(2), .disabled(0)) decoder_11 (
    .out0(decoder_11_out0), .out1(decoder_11_out1), .out2(decoder_11_out2), .out3(decoder_11_out3),
    .sel(in_3[1:0]), .en(decoder_7_out3));
  Register #(.width(32)) register_17 (
    .D(multiplexer_1_out), .en(decoder_8_out0), .Q(register_17_q), .clk(in_6), .clr(in_7));
  Register #(.width(32)) register_18 (
    .D(multiplexer_1_out), .en(decoder_8_out1), .Q(register_18_q), .clk(in_6), .clr(in_7));
  Register #(.width(32)) register_19 (
    .D(multiplexer_1_out), .en(decoder_8_out2), .Q(register_19_q), .clk(in_6), .clr(in_7));
  Register #(.width(32)) register_20 (
    .D(multiplexer_1_out), .en(decoder_8_out3), .Q(register_20_q), .clk(in_6), .clr(in_7));
  Register #(.width(32)) register_21 (
    .D(multiplexer_1_out), .en(decoder_9_out0), .Q(register_21_q), .clk(in_6), .clr(in_7));
  Register #(.width(32)) register_22 (
    .D(multiplexer_1_out), .en(decoder_9_out1), .Q(register_22_q), .clk(in_6), .clr(in_7));
  Register #(.width(32)) register_23 (
    .D(multiplexer_1_out), .en(decoder_9_out2), .Q(register_23_q), .clk(in_6), .clr(in_7));
  Register #(.width(32)) register_24 (
    .D(multiplexer_1_out), .en(decoder_9_out3), .Q(register_24_q), .clk(in_6), .clr(in_7));
  Register #(.width(32)) register_25 (
    .D(multiplexer_1_out), .en(decoder_10_out0), .Q(register_25_q), .clk(in_6), .clr(in_7));
  Register #(.width(32)) register_26 (
    .D(multiplexer_1_out), .en(decoder_10_out1), .Q(register_26_q), .clk(in_6), .clr(in_7));
  Register #(.width(32)) register_27 (
    .D(multiplexer_1_out), .en(decoder_10_out2), .Q(register_27_q), .clk(in_6), .clr(in_7));
  Register #(.width(32)) register_28 (
    .D(multiplexer_1_out), .en(decoder_10_out3), .Q(register_28_q), .clk(in_6), .clr(in_7));
  Register #(.width(32)) register_29 (
    .D(multiplexer_1_out), .en(decoder_11_out0), .Q(register_29_q), .clk(in_6), .clr(in_7));
  Register #(.width(32)) register_30 (
    .D(multiplexer_1_out), .en(decoder_11_out1), .Q(register_30_q), .clk(in_6), .clr(in_7));
  Register #(.width(32)) register_31 (
    .D(multiplexer_1_out), .en(decoder_11_out2), .Q(register_31_q), .clk(in_6), .clr(in_7));
  Register #(.width(32)) register_32 (
    .D(multiplexer_1_out), .en(decoder_11_out3), .Q(register_32_q), .clk(in_6), .clr(in_7));
  Multiplexer #(.select(3), .width(32), .enable("false")) multiplexer_8 (
    .in0(register_17_q), .in1(register_18_q), .in2(register_19_q), .in3(register_20_q), .in4(register_21_q),
    .in5(register_22_q), .in6(register_23_q), .in7(register_24_q), .out(multiplexer_8_out), .sel(in_2[2:0]));
  Multiplexer #(.select(3), .width(32), .enable("false")) multiplexer_9 (
    .in0(register_17_q), .in1(register_18_q), .in2(register_19_q), .in3(register_20_q), .in4(register_21_q),
    .in5(register_22_q), .in6(register_23_q), .in7(register_24_q), .out(multiplexer_9_out), .sel(in_1[2:0]));
  Multiplexer #(.select(3), .width(32), .enable("false")) multiplexer_10 (
    .in0(register_25_q), .in1(register_26_q), .in2(register_27_q), .in3(register_28_q), .in4(register_29_q),
    .in5(register_30_q), .in6(register_31_q), .in7(register_32_q), .out(multiplexer_10_out), .sel(in_2[2:0]));
  Multiplexer #(.select(3), .width(32), .enable("false")) multiplexer_11 (
    .in0(register_25_q), .in1(register_26_q), .in2(register_27_q), .in3(register_28_q), .in4(register_29_q),
    .in5(register_30_q), .in6(register_31_q), .in7(register_32_q), .out(multiplexer_11_out), .sel(in_1[2:0]));
  Multiplexer #(.width(32), .enable("false")) multiplexer_12 (
    .in0(multiplexer_8_out), .in1(multiplexer_10_out), .out(multiplexer_12_out), .sel(in_2[3]));
  Multiplexer #(.width(32), .enable("false")) multiplexer_13 (
    .in0(multiplexer_9_out), .in1(multiplexer_11_out), .out(multiplexer_13_out), .sel(in_1[3]));
  Multiplexer #(.width(32), .enable("false")) multiplexer_14 (
    .in0(multiplexer_6_out), .in1(multiplexer_12_out), .out(out_8), .sel(in_2[4]));
  Multiplexer #(.width(32), .enable("false")) multiplexer_15 (
    .in0(multiplexer_7_out), .in1(multiplexer_13_out), .out(out_9), .sel(in_1[4]));
endmodule
